# Fritzing sketch v2 circuit diagram (saved by Fritzing 0.9.9b)
circuit board: 8.46667cm x 5.64444cm
breadboards: 1

parts:
  Part1 = Arduino Nano (Rev3.0)
  Q1 = npn-Powertransistor [package="TO220 [THT]"]
  R1 = Resistor [tolerance=±5% power=0.25 resistance=1k package=THT]
  D1 = Zener Diode [part_number=1N4732A breakdown_voltage=3.6V package="300 mil [THT]"]
  M2 = gear-motor
  VCC1 = Battery block 9V
  C1 = Ceramic Capacitor [capacitance=1µF voltage=6.3V package="100 mil [THT, multilayer]"]

nets:
  N1: Part1.GND, Q1.emitter, VCC1.-
  N2: Part1.D7, R1.Pin_1
  N3: Q1.base, R1.Pin_0
  N4: Q1.collector, D1.anode, M2.pin_1
  N5: D1.cathode, C1.0
  N6: M2.pin_2, VCC1.+, C1.1
